# Fritzing sketch circuit (saved by Fritzing 0.9.10b)
circuit board: 8.46667cm x 5.64444cm
breadboards: 1

parts:
  Mod1 = Raspberry Pi Pico W
  OLED2 = OLED Mono 0.56 inch blue or white
  U1 = I2C temperature and humidity sensor

nets:
  N1: Mod1.pin_1, OLED2.SDA
  N2: Mod1.pin_2, OLED2.SCL
  GND: Mod1.pin_3, Mod1.pin_8, Mod1.pin_13, Mod1.pin_18, Mod1.pin_23, Mod1.pin_28, Mod1.pin_33, Mod1.pin_38, Mod1.pin_42, OLED2.GND, U1.GND
  N3: Mod1.pin_4, U1.SDA
  N4: Mod1.pin_5, U1.SCL
  VCC: Mod1.pin_36, OLED2.VCC, U1.VDD

notes:
  DHT20 I²C Temperature/Humidity Sensor
  128x32 OLED I²C Display

custom parts:
  Raspberry Pi Pico W: Raspberry Pi Pico W. Based around the RP2040 microcontroller the Pico W is a low cost microcontroller device bringing Raspberry Pi quality, cost, and easy of use to the microcontroller space. The areas marked KEEPOUT in pcb silkscreen should not have traces running through them to avoid shorts on a soldered in module!
  OLED Mono 0.56 inch blue or white: OLED, I2C 3.3V - 5V Blue and White text versions
  I2C temperature and humidity sensor: DHT20 Temperature and Humidity Sensor
